# Fritzing sketch CircuitDesign (saved by Fritzing 0.9.4)

parts:
  U1 = NodeMCU V3.0
  F1 = Fan - 4 wire [package=THT]
  DHT1 = AM2302 DHT22 Humidity and Temperature Sensor

nets:
  N1: U1.D1, F1.Tach
  N2: U1.D2, F1.PWM
  3V3: U1.3V3, DHT1.VCC
  GND: U1.GND, DHT1.GND
  N3: U1.D5, DHT1.DAT

notes:
  To use the buck converter you will conect negative to gnd and positive to the Vin pin.
  The Fan must connect to 12v power. If you're not using the buck converter then you need to bridge the ground to the esp8266 otherwise it will not work properly.

custom parts:
  NodeMCU V3.0: ESP8266 based NodeMCU
  Fan - 4 wire: Fan, 4 wire with tach.
